// Logisim project trabalhoCircuitos.circ as structural Verilog: 14 circuits, main circuit jogo
module jogo (
  input  in_1,
  input  JOGAR,
  input  JOGADOR_0,
  input  in_4,
  input  in_5,
  input  in_6,
  input  in_7,
  input  in_8,
  input  JOGADOR_1,
  input  in_10,
  output A___B,
  output A___B_2,
  output A___B_3
);

  wire decodificador_1_out_5, decodificador_1_out_6, decodificador_1_out_7, decodificador_1_out_8,
       decodificador_1_out_9, decodificador_1_out_10, decodificador_1_out_11, decodificador_1_out_12,
       decodificador_2_out_5, decodificador_2_out_6, decodificador_2_out_7, decodificador_2_out_8,
       decodificador_2_out_9, decodificador_2_out_10, decodificador_2_out_11, decodificador_2_out_12,
       multiplexador4b_1_out_10, multiplexador4b_1_out_11, multiplexador4b_1_out_12, multiplexador4b_1_out_13;

  decodificador decodificador_1 (
    .in_1(JOGADOR_0), .in_2(in_4), .in_3(in_5), .in_4(in_6), .out_5(decodificador_1_out_5),
    .out_6(decodificador_1_out_6), .out_7(decodificador_1_out_7), .out_8(decodificador_1_out_8),
    .out_9(decodificador_1_out_9), .out_10(decodificador_1_out_10), .out_11(decodificador_1_out_11),
    .out_12(decodificador_1_out_12));
  decodificador decodificador_2 (
    .in_1(in_7), .in_2(in_8), .in_3(JOGADOR_1), .in_4(in_10), .out_5(decodificador_2_out_5),
    .out_6(decodificador_2_out_6), .out_7(decodificador_2_out_7), .out_8(decodificador_2_out_8),
    .out_9(decodificador_2_out_9), .out_10(decodificador_2_out_10), .out_11(decodificador_2_out_11),
    .out_12(decodificador_2_out_12));
  _7_Segment_Display u_7_segment_display_1 (
    .g(decodificador_1_out_8), .f(decodificador_1_out_7), .a(decodificador_1_out_6),
    .b(decodificador_1_out_5), .e(decodificador_1_out_9), .d(decodificador_1_out_10),
    .c(decodificador_1_out_11), .dp(decodificador_1_out_12));
  multiplexador4B multiplexador4b_1 (
    .in_1(in_1), .out_10(multiplexador4b_1_out_10), .out_11(multiplexador4b_1_out_11),
    .out_12(multiplexador4b_1_out_12), .out_13(multiplexador4b_1_out_13), .in_2(JOGADOR_0), .in_3(in_4),
    .in_4(in_5), .in_5(in_6), .in_6(in_7), .in_7(in_8), .in_8(JOGADOR_1), .in_9(in_10));
  _7_Segment_Display u_7_segment_display_2 (
    .g(decodificador_2_out_8), .f(decodificador_2_out_7), .a(decodificador_2_out_6),
    .b(decodificador_2_out_5), .e(decodificador_2_out_9), .d(decodificador_2_out_10),
    .c(decodificador_2_out_11), .dp(decodificador_2_out_12));
  comparador comparador_1 (
    .in_2(multiplexador4b_1_out_10), .in_3(multiplexador4b_1_out_11), .in_4(multiplexador4b_1_out_12),
    .in_5(multiplexador4b_1_out_13), .in_1(JOGAR), .out_6(A___B), .A___B(A___B_2), .A___B_2(A___B_3));

  // Notes on the sheet:
  //   ESCOLHA DO
  //   JOGADOR 0
  //   JOGADOR DA VEZ (A)
  //   ESCOLHA DO
  //   JOGADOR 1
endmodule

// COMP.
module comparador (
  input  in_1,
  input  in_2,
  input  in_3,
  input  in_4,
  input  in_5,
  output out_6,
  output A___B,
  output A___B_2
);

  wire and_1_out, and_2_out, and_3_out, and_4_out, and_5_out, not_1_out, not_2_out, not_3_out, not_4_out,
       not_5_out, or_1_out, or_2_out, portaxnor_1_out_3, portaxnor_2_out_3, portaxnor_3_out_3,
       portaxnor_4_out_3;

  portaXNOR portaxnor_1 (.in_1(in_2), .out_3(portaxnor_1_out_3), .in_2(1'b0));
  portaXNOR portaxnor_2 (.in_1(in_3), .out_3(portaxnor_2_out_3), .in_2(1'b1));
  portaXNOR portaxnor_3 (.in_1(in_4), .out_3(portaxnor_3_out_3), .in_2(1'b1));
  portaXNOR portaxnor_4 (.in_1(in_5), .out_3(portaxnor_4_out_3), .in_2(1'b0));
  not not_1 (not_1_out, 1'b0);
  not not_2 (not_2_out, 1'b1);
  not not_3 (not_3_out, 1'b1);
  not not_4 (not_4_out, 1'b0);
  and and_1 (and_1_out, in_2, not_1_out);
  and and_2 (and_2_out, in_3, portaxnor_1_out_3, not_2_out);
  and and_3 (and_3_out, in_4, portaxnor_1_out_3, portaxnor_2_out_3, not_3_out);
  and and_4 (and_4_out, in_5, portaxnor_1_out_3, portaxnor_2_out_3, portaxnor_3_out_3, not_4_out);
  and and_5 (and_5_out, portaxnor_1_out_3, portaxnor_2_out_3, portaxnor_3_out_3, portaxnor_4_out_3);
  or or_1 (or_1_out, and_1_out, and_2_out, and_3_out, and_4_out);
  not not_5 (not_5_out, or_2_out);
  or or_2 (or_2_out, and_5_out, or_1_out);
  and and_6 (out_6, in_1, and_5_out);
  and and_7 (A___B, in_1, or_1_out);
  and and_8 (A___B_2, in_1, not_5_out);
endmodule

module portaXOR (
  input  in_1,
  input  in_2,
  output out_3
);

  wire and_1_out, and_2_out, not_1_out, not_2_out, or_1_out;

  not not_1 (not_1_out, in_1);
  not not_2 (not_2_out, in_2);
  and and_1 (and_1_out, in_1, in_2);
  and and_2 (and_2_out, not_1_out, not_2_out);
  or or_1 (or_1_out, and_1_out, and_2_out);
  not not_3 (out_3, or_1_out);
endmodule

// XNOR
module portaXNOR (
  input  in_1,
  input  in_2,
  output out_3
);

  wire portaxor_1_out_3;

  portaXOR portaxor_1 (.in_1(in_1), .in_2(in_2), .out_3(portaxor_1_out_3));
  not not_1 (out_3, portaxor_1_out_3);
endmodule

// MULTIPLEX.
module multiplexador4B (
  input  in_1,
  input  in_2,
  input  in_3,
  input  in_4,
  input  in_5,
  input  in_6,
  input  in_7,
  input  in_8,
  input  in_9,
  output out_10,
  output out_11,
  output out_12,
  output out_13
);

  wire and_1_out, and_2_out, and_3_out, and_4_out, and_5_out, and_6_out, and_7_out, and_8_out;

  and and_1 (and_1_out, in_2, ~in_1);  // AND_Gate
  and and_2 (and_2_out, in_1, in_6);
  and and_3 (and_3_out, in_3, ~in_1);  // AND_Gate
  and and_4 (and_4_out, in_1, in_7);
  and and_5 (and_5_out, in_4, ~in_1);  // AND_Gate
  and and_6 (and_6_out, in_1, in_8);
  and and_7 (and_7_out, in_5, ~in_1);  // AND_Gate
  and and_8 (and_8_out, in_1, in_9);
  or or_1 (out_10, and_1_out, and_2_out);
  or or_2 (out_11, and_3_out, and_4_out);
  or or_3 (out_12, and_5_out, and_6_out);
  or or_4 (out_13, and_7_out, and_8_out);
endmodule

// a
module displayA (
  input  in_1,
  input  in_2,
  input  in_3,
  input  in_4,
  output out_5
);

  wire and_1_out, and_2_out, and_3_out, and_4_out, and_5_out;

  and and_1 (and_1_out, ~in_1, in_2, ~in_3);  // AND_Gate
  and and_2 (and_2_out, in_1, in_4);
  and and_3 (and_3_out, ~in_2, in_3);  // AND_Gate
  and and_4 (and_4_out, in_1, ~in_2);  // AND_Gate
  and and_5 (and_5_out, in_3, ~in_4);  // AND_Gate
  or or_1 (out_5, and_1_out, and_2_out, and_3_out, and_4_out, and_5_out);
endmodule

// b
module displayB (
  input  in_1,
  input  in_2,
  input  in_3,
  input  in_4,
  output out_5
);

  wire and_1_out, and_2_out, and_3_out, and_4_out, and_5_out;

  and and_1 (and_1_out, ~in_1, in_2, ~in_3);  // AND_Gate
  and and_2 (and_2_out, in_2, ~in_4);  // AND_Gate
  and and_3 (and_3_out, ~in_3, ~in_4);  // AND_Gate
  and and_4 (and_4_out, in_1, ~in_2);  // AND_Gate
  and and_5 (and_5_out, in_1, in_3);
  or or_1 (out_5, and_1_out, and_2_out, and_3_out, and_4_out, and_5_out);
endmodule

// c
module displayC (
  input  in_1,
  input  in_2,
  input  in_3,
  input  in_4,
  output out_5
);

  wire and_1_out, and_2_out, and_3_out, and_4_out, and_5_out, and_6_out;

  and and_1 (and_1_out, ~in_1, in_2, in_4);  // AND_Gate
  and and_2 (and_2_out, in_1, ~in_2, ~in_3);  // AND_Gate
  and and_3 (and_3_out, in_1, ~in_4);  // AND_Gate
  and and_4 (and_4_out, ~in_2, ~in_4);  // AND_Gate
  and and_5 (and_5_out, ~in_1, in_3);  // AND_Gate
  and and_6 (and_6_out, in_2, in_3);
  or or_1 (out_5, and_1_out, and_2_out, and_3_out, and_4_out, and_5_out, and_6_out);
endmodule

// d
module displayD (
  input  in_1,
  input  in_2,
  input  in_3,
  input  in_4,
  output out_5
);

  wire and_1_out, and_2_out, and_3_out, and_4_out, and_5_out;

  and and_1 (and_1_out, ~in_1, ~in_3, ~in_4);  // AND_Gate
  and and_2 (and_2_out, in_1, ~in_3, in_4);  // AND_Gate
  and and_3 (and_3_out, ~in_1, in_3, in_4);  // AND_Gate
  and and_4 (and_4_out, ~in_2, ~in_3);  // AND_Gate
  and and_5 (and_5_out, ~in_2, ~in_4);  // AND_Gate
  or or_1 (out_5, and_1_out, and_2_out, and_3_out, and_4_out, and_5_out);
endmodule

// e
module displayE (
  input  in_1,
  input  in_2,
  input  in_3,
  input  in_4,
  output out_5
);

  wire and_1_out;

  and and_1 (and_1_out, in_1, ~in_1);  // AND_Gate
  and and_2 (out_5, in_4, in_3, in_2, and_1_out);
endmodule

// f
module displayF (
  input  in_1,
  input  in_2,
  input  in_3,
  input  in_4,
  output out_5
);

  wire and_1_out, and_2_out, and_3_out, and_4_out, and_5_out;

  and and_1 (and_1_out, ~in_1, ~in_3);  // AND_Gate
  and and_2 (and_2_out, ~in_1, in_4);  // AND_Gate
  and and_3 (and_3_out, ~in_3, in_4);  // AND_Gate
  and and_4 (and_4_out, ~in_1, in_2);  // AND_Gate
  and and_5 (and_5_out, in_1, ~in_2);  // AND_Gate
  or or_1 (out_5, and_1_out, and_2_out, and_3_out, and_4_out, and_5_out);
endmodule

// g
module displayG (
  input  in_1,
  input  in_2,
  input  in_3,
  input  in_4,
  output out_5
);

  wire and_1_out, and_2_out, and_3_out, and_4_out, and_5_out, and_6_out;

  and and_1 (and_1_out, ~in_1, ~in_2, ~in_4);  // AND_Gate
  and and_2 (and_2_out, ~in_1, ~in_2, in_3);  // AND_Gate
  and and_3 (and_3_out, in_2, ~in_3, in_4);  // AND_Gate
  and and_4 (and_4_out, in_2, in_3, ~in_4);  // AND_Gate
  and and_5 (and_5_out, in_1, ~in_2, in_4);  // AND_Gate
  and and_6 (and_6_out, in_1, ~in_3);  // AND_Gate
  or or_1 (out_5, and_1_out, and_2_out, and_3_out, and_4_out, and_5_out, and_6_out);
endmodule

// h
module displayH (
  input  in_1,
  input  in_2,
  input  in_3,
  input  in_4,
  output out_5
);

  wire and_1_out, and_2_out, and_3_out, and_4_out;

  and and_1 (and_1_out, ~in_2, ~in_4);  // AND_Gate
  and and_2 (and_2_out, in_1, in_3);
  and and_3 (and_3_out, in_1, in_2);
  and and_4 (and_4_out, in_3, ~in_4);  // AND_Gate
  or or_1 (out_5, and_1_out, and_2_out, and_3_out, and_4_out);
endmodule

// DECODIF.
module decodificador (
  input  in_1,
  input  in_2,
  input  in_3,
  input  in_4,
  output out_5,
  output out_6,
  output out_7,
  output out_8,
  output out_9,
  output out_10,
  output out_11,
  output out_12
);

  displayD displayd_1 (.in_1(in_1), .in_2(in_2), .in_3(in_3), .in_4(in_4), .out_5(out_5));
  displayC displayc_1 (.in_1(in_1), .in_2(in_2), .in_3(in_3), .in_4(in_4), .out_5(out_6));
  displayB displayb_1 (.in_1(in_1), .in_2(in_2), .in_3(in_3), .in_4(in_4), .out_5(out_7));
  displayA displaya_1 (.in_1(in_1), .in_2(in_2), .in_3(in_3), .in_4(in_4), .out_5(out_8));
  displayH displayh_1 (.in_1(in_1), .in_2(in_2), .in_3(in_3), .in_4(in_4), .out_5(out_9));
  displayG displayg_1 (.in_1(in_1), .in_2(in_2), .in_3(in_3), .in_4(in_4), .out_5(out_10));
  displayF displayf_1 (.in_1(in_1), .in_2(in_2), .in_3(in_3), .in_4(in_4), .out_5(out_11));
  displayE displaye_1 (.in_1(in_1), .in_2(in_2), .in_3(in_3), .in_4(in_4), .out_5(out_12));
endmodule
